# Fritzing sketch LaserCommunicator (saved by Fritzing 0.9.3b)
breadboards: 2

parts:
  LD1 = LD
  R1 = Resistor [tolerance=±5% resistance=220 package=THT]
  SP1 = SPEAKER [package=pcb_mount_speaker]
  U1 = 3.5mm Audio Jack [package=audio-jack]
  R2 = Resistor [tolerance=±5% resistance=220 package=THT]
  Photp_résistance = Photocell (LDR) [package=THT]
  R3 = Resistor [tolerance=±5% resistance=1k package=THT]
  BAT1 = BC9VPC [package=bc9vpc]
  BAT2 = BC9VPC [package=bc9vpc]

nets:
  N1: LD1.cathode, U1.SLEEVE, R2.Pin_0, BAT2.V-
  N2: LD1.anode, R1.Pin_1
  N3: R1.Pin_0, U1.LEFT, R2.Pin_1, BAT2.V+
  N4: SP1.+, R3.Pin_0, BAT1.V-
  N5: SP1.-, Photp_résistance.pin_1, R3.Pin_1
  N6: Photp_résistance.pin_0, BAT1.V+

custom parts:
  LD: A Generic Red Dot Laser Diode Module (~5mW)
